// Digital circuit ControlUnit.dig as structural Verilog
module ControlUnit (
  input  [5:0] inst,
  output [3:0] alu
);

  wire comparator_1_eq, comparator_2_eq;
  wire [3:0] demultiplexer_1_out_2;

  Demultiplexer #(.Selector_Bits(2), .Bits(4)) demultiplexer_1 (
    .sel(inst[5:4]), .in(inst[3:0]), .out_0(alu), .out_2(demultiplexer_1_out_2));  // open: out_1, out_3
  Comparator #(.Bits(4)) comparator_1 (.a(demultiplexer_1_out_2), .b(4'b1011), .eq(comparator_1_eq));  // open: gt, lt
  Comparator #(.Bits(4)) comparator_2 (.a(demultiplexer_1_out_2), .b(4'b1010), .eq(comparator_2_eq));  // open: gt, lt

  // Notes on the sheet:
  //   disable writing to reg when op is 000000
endmodule
