// Digital circuit dustcat-III.dig as structural Verilog
module dustcat_III (
  input  clk,
  output [23:0] program_addr
);

  wire program_reset_out, pulldown_1_out, undriven;
  wire [1:0] undriven_3;
  wire [3:0] undriven_2;
  wire [4:0] decoder_1_dest, decoder_1_src1, decoder_1_src2, multiplexer_1_out;
  wire [5:0] decoder_1_op;
  wire [15:0] decoder_1_const;
  wire [23:0] pulldown_2_out;
  wire [31:0] alu_1_out, eepromdualport_1_d, multiplexer_2_out, registerfile_1_db;
  wire [31:24] registerfile_1_da;

  Button program_reset (.out(program_reset_out));
  PullDown pulldown_1 (.out(pulldown_1_out));
  PullDown #(.Bits(24)) pulldown_2 (.out(pulldown_2_out));
  CounterPreset #(.Bits(24)) counterpreset_1 (
    .en(1'b1), .C(clk), .dir(1'b0), .in(pulldown_2_out), .ld(pulldown_1_out), .clr(program_reset_out),
    .out(program_addr));  // open: ovf
  EEPROMDualPort #(.AddrBits(24), .isProgramMemory("true"), .Bits(32)) eepromdualport_1 (
    .A(program_addr), .Din({32{1'b0}}), .str(1'b0), .C(clk), .ld(1'b1), .D(eepromdualport_1_d));
  decoder decoder_1 (
    .inst(eepromdualport_1_d), .\const (decoder_1_const), .OP(decoder_1_op), .DEST(decoder_1_dest),
    .SRC1(decoder_1_src1), .SRC2(decoder_1_src2));
  Multiplexer #(.Bits(5)) multiplexer_1 (
    .sel(undriven), .in_0(decoder_1_src1), .in_1(decoder_1_dest), .out(multiplexer_1_out));
  RegisterFile #(.AddrBits(5), .Bits(32)) registerfile_1 (
    .Din(multiplexer_2_out), .we(1'b1), .Rw(decoder_1_dest), .C(clk), .Ra(multiplexer_1_out),
    .Rb(decoder_1_src2), .Da({registerfile_1_da, pulldown_2_out}), .Db(registerfile_1_db));
  alu alu_1 (
    .A({registerfile_1_da, pulldown_2_out}), .B(registerfile_1_db), .OP(undriven_2), .out(alu_1_out));  // open: overflow
  ScopeStack scopestack_1 ();  // open: cAd, curAd, call, fRet, clear, sovf, lAd, add
  Multiplexer #(.Selector_Bits(2), .Bits(32)) multiplexer_2 (
    .sel(undriven_3), .in_0(alu_1_out), .in_1({{16{1'b0}}, decoder_1_const}),
    .in_2({decoder_1_const, alu_1_out[15:0]}), .in_3(alu_1_out), .out(multiplexer_2_out));

  // Notes on the sheet:
  //   clk: Hz: 50000
  //   contents of eepromdualport_1 (hex, n*v repeats v):
  //   ac200010,d8010000,ace00005,b8070000,bc000000,ada00002,35cd0010,25ce0002,b40b7000,
  //   25ce0001,b40c7000,25ce0001,b40a7000,29ce0003,b40a7000,bc000000,ad40ffff,ad60000f,
  //   ad8000af,ace00005,b8070000,ade00000,ac200019,c40f0800,ad200022,ad00001c,c8080000,
  //   d8090000,25ef0001,256b0001,ace00005,b8070000,ac600016,d8030000
endmodule
